# Fritzing sketch genius (saved by Fritzing 0.9.3b)
breadboards: 1

parts:
  Part1 = Arduino Uno (Rev3)
  LED1 = smd LED [color="Blue (430nm)" package="1206 [SMD]"]
  R1 = Resistor [tolerance=±5% resistance=220 package="2010 [SMD]"]
  S1 = Pushbutton [package="[THT]"]
  LED2 = smd LED [color="Green (560nm)" package="1206 [SMD]"]
  LED3 = smd LED [color="Red (633nm)" package="1206 [SMD]"]
  R3 = Resistor [tolerance=±5% resistance=220 package="2010 [SMD]"]
  R4 = Resistor [tolerance=±5% resistance=220 package="2010 [SMD]"]
  S2 = Pushbutton [package="[THT]"]
  S3 = Pushbutton [package="[THT]"]
  U1 = POT [package=pot_alpha_rv16af-20]

nets:
  N1: Part1.A0, U1.S
  N2: Part1.D8, S3.Pin_3, S3.Pin_4
  N3: Part1.D9_PWM, S2.Pin_3, S2.Pin_4
  N4: Part1.D10_PWM/SS, Part1.GND, R1.Pin_0, S1.Pin_1, S1.Pin_2, R3.Pin_0, R4.Pin_0, S2.Pin_1, S2.Pin_2, S3.Pin_1, S3.Pin_2, U1.A
  N5: Part1.D2, LED1.anode
  N6: Part1.D3_PWM, LED2.anode
  N7: Part1.D4, LED3.anode
  N8: Part1.5V, U1.E
  N9: LED1.cathode, R1.Pin_1
  N10: S1.Pin_3, S1.Pin_4
  N11: LED2.cathode, R3.Pin_1
  N12: LED3.cathode, R4.Pin_1
